# Fritzing sketch LogoBot (saved by Fritzing 0.9.0b)
circuit board: 8.46667cm x 5.64444cm
breadboards: 1

parts:
  RGB_Pipe_Light = RGB LED (com. cathode, rgb) [package="5 mm [THT]"]
  Piezo_Sounder = Piezo Speaker
  Stepper_Right = ULN2003A [package="DIP16 [THT]"]
  Stepper_Left = ULN2003A [package="DIP16 [THT]"]
  WiFi_or_BT_UART = Header 2 [package=springterminal-2.54mm-2]
  Bump_Switches = Header 4 [package=1x04-1mm-ra]
  Arduino_Pro_Mini = Arduino Mini (Rev5)

nets:
  N1: RGB_Pipe_Light.red_anode, Arduino_Pro_Mini.D6_PWM
  N2: RGB_Pipe_Light.green_anode, Arduino_Pro_Mini.D3_PWM
  N3: RGB_Pipe_Light.blue_anode, Arduino_Pro_Mini.D5_PWM
  N4: Piezo_Sounder.pin2, Arduino_Pro_Mini.D4
  N5: Stepper_Right.In_1, Arduino_Pro_Mini.D13
  N6: Stepper_Right.In_2, Arduino_Pro_Mini.D12
  N7: Stepper_Right.In_3, Arduino_Pro_Mini.D8
  N8: Stepper_Right.In_4, Arduino_Pro_Mini.D7
  N9: Stepper_Left.In_1, Arduino_Pro_Mini.A0
  N10: Stepper_Left.In_2, Arduino_Pro_Mini.A1
  N11: Stepper_Left.In_3, Arduino_Pro_Mini.A2
  N12: Stepper_Left.In_4, Arduino_Pro_Mini.A3
  N13: WiFi_or_BT_UART.1, Arduino_Pro_Mini.D1/RX, Arduino_Pro_Mini.RX
  N14: WiFi_or_BT_UART.2, Arduino_Pro_Mini.D0/TX
  N15: Bump_Switches.1, Arduino_Pro_Mini.A4
  N16: Bump_Switches.2, Arduino_Pro_Mini.A5
  N17: Bump_Switches.3, Arduino_Pro_Mini.A6
  N18: Bump_Switches.4, Arduino_Pro_Mini.A7
